# Fritzing sketch botao_led (saved by Fritzing 0.9.2b)
breadboards: 1

parts:
  R1 = Resistor [tolerance=±5% resistance=220 package=THT]
  LED1 = LED - 5mm [color="Red (633nm)" package="5 mm [THT]"]
  R3 = Resistor [tolerance=±5% resistance=10k package=THT]
  S1 = Pushbutton [package="[THT]"]
  Part1 = Arduino Uno (Rev3)

nets:
  N1: R1.Pin_0, LED1.anode
  N2: R1.Pin_1, Part1.D12/MISO
  N3: LED1.cathode, R3.Pin_0, Part1.GND
  N4: R3.Pin_1, S1.Pin_3, S1.Pin_4, Part1.D7
  N5: S1.Pin_1, S1.Pin_2, Part1.5V
