# Fritzing sketch fotoresistor_ldr_read (saved by Fritzing 0.9.2b)
breadboards: 1

parts:
  R1 = Resistor [tolerance=±5% resistance=10k package=THT]
  R2 = Photocell (LDR) [package=THT]
  Part1 = Arduino Uno (Rev3)

nets:
  N1: R1.Pin_0, Part1.5V
  N2: R1.Pin_1, R2.pin_0, Part1.A0
  N3: R2.pin_1, Part1.GND
