# Fritzing sketch analog_change_led_intensity (saved by Fritzing 0.9.2b)
breadboards: 1

parts:
  Componente1 = Arduino Mega 2560 (Rev3)
  R1 = Resistor [tolerance=±5% resistance=220 package=THT]
  LED1 = LED - 5mm [color="Red (633nm)" package="5 mm [THT]"]
  R2 = Photocell (LDR) [package=THT]
  R3 = Resistor [tolerance=±5% resistance=220 package=THT]

nets:
  N1: Componente1.A0, R2.pin_0, R3.Pin_1
  N2: Componente1.GND, LED1.cathode, R3.Pin_0
  N3: Componente1.D12_PWM, R1.Pin_1
  N4: Componente1.5V, R2.pin_1
  N5: R1.Pin_0, LED1.anode
