# Fritzing sketch analog_pwm (saved by Fritzing 0.9.2b)
breadboards: 1

parts:
  Componente1 = Arduino Mega 2560 (Rev3)
  R1 = Resistor [tolerance=±5% resistance=220 package=THT]
  LED1 = LED - 5mm [color="Red (633nm)" package="5 mm [THT]"]

nets:
  N1: Componente1.GND, LED1.cathode
  N2: Componente1.D12_PWM, R1.Pin_1
  N3: R1.Pin_0, LED1.anode
