# Fritzing sketch higrometro (saved by Fritzing 0.9.3b)
breadboards: 1

parts:
  Part13 = FC-28 Soil Hygrometer Module - Probe
  Part14 = FC-28 Soil Hygrometer Module
  Part15 = Arduino Uno (Rev3)
  LED3 = smd LED [color="Green (555nm)" package="0603 [SMD]"]
  LED4 = smd LED [color="Red (633nm)" package="0603 [SMD]"]
  R6 = Resistor [tolerance=±5% resistance=150 package=THT]
  R7 = Resistor [tolerance=±5% resistance=220 package=THT]
  LCM1602_IIC7 = LCM1602 IIC [part_number="LCM1602 IIC" chip_label="LCM1602 IIC" package="DIP (Dual Inline) [THT]"]
  LCD7 = LCD screen

nets:
  N1: Part13.POS, Part14.POS
  N2: Part13.NEG, Part14.NEG
  VCC: Part14.VCC, LCM1602_IIC7.VCC
  GND: Part14.GND, LED3.cathode, LED4.cathode, LCM1602_IIC7.GND
  N3: Part14.AO, Part15.A1
  N4: Part15.D12/MISO, R7.Pin_1
  N5: Part15.D13/SCK, R6.Pin_1
  N6: Part15.A4/SDA, LCM1602_IIC7.SDA
  N7: Part15.A5/SCL, LCM1602_IIC7.SCL
  N8: LED3.anode, R7.Pin_0
  N9: LED4.anode, R6.Pin_0
  VSS: LCM1602_IIC7.VSS, LCD7.VSS
  VDD: LCM1602_IIC7.VDD, LCD7.VDD
  N10: LCM1602_IIC7.V0, LCD7.V0
  N11: LCM1602_IIC7.RS, LCD7.RS
  N12: LCM1602_IIC7.RW, LCD7.R/W
  N13: LCM1602_IIC7.E, LCD7.E
  N14: LCM1602_IIC7.D0, LCD7.DB0
  N15: LCM1602_IIC7.D1, LCD7.DB1
  N16: LCM1602_IIC7.D2, LCD7.DB2
  N17: LCM1602_IIC7.D3, LCD7.DB3
  N18: LCM1602_IIC7.D4, LCD7.DB4
  N19: LCM1602_IIC7.D5, LCD7.DB5
  N20: LCM1602_IIC7.D6, LCD7.DB6
  N21: LCM1602_IIC7.D7, LCD7.DB7
  N22: LCM1602_IIC7.A, LCD7.LED+
  N23: LCM1602_IIC7.K, LCD7.LED-

custom parts:
  FC-28 Soil Hygrometer Module - Probe: The FC-28 is a soil hygrometer module that uses the Texas Instruments LM393 comparator chip to provide an analog measurement of soil humidity.
  FC-28 Soil Hygrometer Module: The FC-28 is a soil hygrometer module that uses the Texas Instruments LM393 comparator chip to provide an analog measurement of soil humidity. The digital output is high when soil moisture is over a certain threshold, as determined by adjusting the potentiometer.
  LCM1602 IIC: I2C-Module to use a 1602 or 2004 LCD on with the wire.h libory Serial LCD Modul
