# Fritzing sketch led_rgb (saved by Fritzing 0.9.2b)
breadboards: 1

parts:
  LED1 = RGB LED (com. cathode, rgb) [package="5 mm [THT]"]
  R1 = Resistor [tolerance=±5% resistance=150 package=THT]
  R2 = Resistor [tolerance=±5% resistance=100 package=THT]
  R3 = Resistor [tolerance=±5% resistance=100 package=THT]
  Part1 = Arduino Uno (Rev3)

nets:
  N1: LED1.red_anode, R2.Pin_0
  N2: LED1.common_cathode, R3.Pin_0
  N3: LED1.green_anode, Part1.GND
  N4: LED1.blue_anode, R1.Pin_0
  N5: R1.Pin_1, Part1.D9_PWM
  N6: R2.Pin_1, Part1.D11_PWM/MOSI
  N7: R3.Pin_1, Part1.D10_PWM/SS
