# Fritzing sketch lm35dz_sensor (saved by Fritzing 0.9.3b)
breadboards: 1

parts:
  T1 = LM35 Temperature Sensor [package="TO92 [THT]"]
  Part1 = Arduino Uno (Rev3)
  LCM1602_IIC6 = LCM1602 IIC [part_number="LCM1602 IIC" chip_label="LCM1602 IIC" package="DIP (Dual Inline) [THT]"]
  LCD6 = LCD screen

nets:
  5V: T1.+Vs, Part1.5V, LCM1602_IIC6.VCC
  N1: T1.Vout, Part1.A2
  GND: T1.GND, Part1.GND, LCM1602_IIC6.GND
  N2: Part1.A4/SDA, LCM1602_IIC6.SDA
  N3: Part1.A5/SCL, LCM1602_IIC6.SCL
  VSS: LCM1602_IIC6.VSS, LCD6.VSS
  VDD: LCM1602_IIC6.VDD, LCD6.VDD
  N4: LCM1602_IIC6.V0, LCD6.V0
  N5: LCM1602_IIC6.RS, LCD6.RS
  N6: LCM1602_IIC6.RW, LCD6.R/W
  N7: LCM1602_IIC6.E, LCD6.E
  N8: LCM1602_IIC6.D0, LCD6.DB0
  N9: LCM1602_IIC6.D1, LCD6.DB1
  N10: LCM1602_IIC6.D2, LCD6.DB2
  N11: LCM1602_IIC6.D3, LCD6.DB3
  N12: LCM1602_IIC6.D4, LCD6.DB4
  N13: LCM1602_IIC6.D5, LCD6.DB5
  N14: LCM1602_IIC6.D6, LCD6.DB6
  N15: LCM1602_IIC6.D7, LCD6.DB7
  N16: LCM1602_IIC6.A, LCD6.LED+
  N17: LCM1602_IIC6.K, LCD6.LED-

custom parts:
  LCM1602 IIC: I2C-Module to use a 1602 or 2004 LCD on with the wire.h libory Serial LCD Modul
