# Fritzing sketch semaforo_interativo (saved by Fritzing 0.9.2b)
breadboards: 1

parts:
  LED1 = LED - 5mm [color="Green (555nm)" package="5 mm [THT]"]
  LED2 = LED - 5mm [color="Yellow (595nm)" package="5 mm [THT]"]
  R1 = Resistor [tolerance=±5% resistance=220 package=THT]
  LED3 = LED - 5mm [color="Red (633nm)" package="5 mm [THT]"]
  R2 = Resistor [tolerance=±5% resistance=220 package=THT]
  R3 = Resistor [tolerance=±5% resistance=220 package=THT]
  S1 = Pushbutton [package="[THT]"]
  LED4 = LED - 5mm [color="Green (555nm)" package="5 mm [THT]"]
  R4 = Resistor [tolerance=±5% resistance=220 package=THT]
  LED5 = LED - 5mm [color="Red (633nm)" package="5 mm [THT]"]
  R5 = Resistor [tolerance=±5% resistance=220 package=THT]
  Part1 = Arduino Uno (Rev3)
  R6 = Resistor [tolerance=±5% resistance=10k package=THT]

nets:
  N1: LED1.cathode, LED2.cathode, LED3.cathode, LED4.cathode, LED5.cathode, Part1.GND, R6.Pin_0
  N2: LED1.anode, R1.Pin_0
  N3: LED2.anode, R2.Pin_0
  N4: R1.Pin_1, Part1.D10_PWM/SS
  N5: LED3.anode, R3.Pin_0
  N6: R2.Pin_1, Part1.D9_PWM
  N7: R3.Pin_1, Part1.D8
  N8: S1.Pin_1, S1.Pin_2, Part1.5V
  N9: S1.Pin_3, S1.Pin_4, Part1.D7, R6.Pin_1
  N10: LED4.anode, R4.Pin_0
  N11: R4.Pin_1, Part1.D6_PWM
  N12: LED5.anode, R5.Pin_0
  N13: R5.Pin_1, Part1.D5_PWM
