# Fritzing sketch sensor_de_molhamento (saved by Fritzing 0.9.3b)
breadboards: 1

parts:
  Part1 = Humidity Sensor - HIH-4030 Breakout
  Part2 = Arduino Uno (Rev3)
  LCM1602_IIC4 = LCM1602 IIC [part_number="LCM1602 IIC" chip_label="LCM1602 IIC" package="DIP (Dual Inline) [THT]"]
  LCD4 = LCD screen

nets:
  GND: Part1.GND, Part2.GND, LCM1602_IIC4.GND
  N1: Part1.OUT, Part2.A0
  VCC: Part1.VCC, Part2.5V, LCM1602_IIC4.VCC
  N2: Part2.A4/SDA, LCM1602_IIC4.SDA
  N3: Part2.A5/SCL, LCM1602_IIC4.SCL
  VSS: LCM1602_IIC4.VSS, LCD4.VSS
  VDD: LCM1602_IIC4.VDD, LCD4.VDD
  N4: LCM1602_IIC4.V0, LCD4.V0
  N5: LCM1602_IIC4.RS, LCD4.RS
  N6: LCM1602_IIC4.RW, LCD4.R/W
  N7: LCM1602_IIC4.E, LCD4.E
  N8: LCM1602_IIC4.D0, LCD4.DB0
  N9: LCM1602_IIC4.D1, LCD4.DB1
  N10: LCM1602_IIC4.D2, LCD4.DB2
  N11: LCM1602_IIC4.D3, LCD4.DB3
  N12: LCM1602_IIC4.D4, LCD4.DB4
  N13: LCM1602_IIC4.D5, LCD4.DB5
  N14: LCM1602_IIC4.D6, LCD4.DB6
  N15: LCM1602_IIC4.D7, LCD4.DB7
  N16: LCM1602_IIC4.A, LCD4.LED+
  N17: LCM1602_IIC4.K, LCD4.LED-

custom parts:
  LCM1602 IIC: I2C-Module to use a 1602 or 2004 LCD on with the wire.h libory Serial LCD Modul
