# Fritzing sketch fotoresistor_led_inteligente (saved by Fritzing 0.9.2b)
breadboards: 1

parts:
  Part2 = Arduino Uno (Rev3)
  R3 = Resistor [tolerance=±5% resistance=10k package=THT]
  R4 = Photocell (LDR) [package=THT]
  LED1 = LED - 5mm [color="Red (633nm)" package="5 mm [THT]"]
  R5 = Resistor [tolerance=±5% resistance=220 package=THT]

nets:
  N1: Part2.A0, R3.Pin_1, R4.pin_0
  N2: Part2.GND, R4.pin_1, LED1.cathode
  N3: Part2.D2, R5.Pin_1
  N4: Part2.5V, R3.Pin_0
  N5: LED1.anode, R5.Pin_0
