# Fritzing sketch dht22_sensor (saved by Fritzing 0.9.3b)
breadboards: 1

parts:
  DHT1 = DHT22 Humidity and Temperature Sensor
  R1 = Resistor [tolerance=±5% resistance=10k package=THT]
  Part6 = Arduino Uno (Rev3)
  LCM1602_IIC5 = LCM1602 IIC [part_number="LCM1602 IIC" chip_label="LCM1602 IIC" package="DIP (Dual Inline) [THT]"]
  LCD5 = LCD screen

nets:
  VDD: DHT1.VDD, R1.Pin_0, Part6.5V, LCM1602_IIC5.VCC
  N1: DHT1.DATA, R1.Pin_1, Part6.D10_PWM/SS
  GND: DHT1.GND, Part6.GND, LCM1602_IIC5.GND
  N2: Part6.A4/SDA, LCM1602_IIC5.SDA
  N3: Part6.A5/SCL, LCM1602_IIC5.SCL
  VSS: LCM1602_IIC5.VSS, LCD5.VSS
  VDD_2: LCM1602_IIC5.VDD, LCD5.VDD
  N4: LCM1602_IIC5.V0, LCD5.V0
  N5: LCM1602_IIC5.RS, LCD5.RS
  N6: LCM1602_IIC5.RW, LCD5.R/W
  N7: LCM1602_IIC5.E, LCD5.E
  N8: LCM1602_IIC5.D0, LCD5.DB0
  N9: LCM1602_IIC5.D1, LCD5.DB1
  N10: LCM1602_IIC5.D2, LCD5.DB2
  N11: LCM1602_IIC5.D3, LCD5.DB3
  N12: LCM1602_IIC5.D4, LCD5.DB4
  N13: LCM1602_IIC5.D5, LCD5.DB5
  N14: LCM1602_IIC5.D6, LCD5.DB6
  N15: LCM1602_IIC5.D7, LCD5.DB7
  N16: LCM1602_IIC5.A, LCD5.LED+
  N17: LCM1602_IIC5.K, LCD5.LED-

custom parts:
  LCM1602 IIC: I2C-Module to use a 1602 or 2004 LCD on with the wire.h libory Serial LCD Modul
