# Fritzing sketch sd_card (saved by Fritzing 0.9.3b)
breadboards: 1

parts:
  LCM1602_IIC2 = LCM1602 IIC [part_number="LCM1602 IIC" chip_label="LCM1602 IIC" package="DIP (Dual Inline) [THT]"]
  LCD2 = LCD screen
  SD_card_module1 = SD Card Module
  Part4 = Logic Level Converter
  Part5 = Arduino Uno (Rev3)
  Part3 = Humidity Sensor - HIH-4030 Breakout

nets:
  VSS: LCM1602_IIC2.VSS, LCD2.VSS
  VDD: LCM1602_IIC2.VDD, LCD2.VDD
  N1: LCM1602_IIC2.V0, LCD2.V0
  N2: LCM1602_IIC2.RS, LCD2.RS
  N3: LCM1602_IIC2.RW, LCD2.R/W
  N4: LCM1602_IIC2.E, LCD2.E
  N5: LCM1602_IIC2.D0, LCD2.DB0
  N6: LCM1602_IIC2.D1, LCD2.DB1
  N7: LCM1602_IIC2.D2, LCD2.DB2
  N8: LCM1602_IIC2.D3, LCD2.DB3
  N9: LCM1602_IIC2.D4, LCD2.DB4
  N10: LCM1602_IIC2.D5, LCD2.DB5
  N11: LCM1602_IIC2.D6, LCD2.DB6
  N12: LCM1602_IIC2.D7, LCD2.DB7
  N13: LCM1602_IIC2.A, LCD2.LED+
  N14: LCM1602_IIC2.K, LCD2.LED-
  GND: LCM1602_IIC2.GND, Part4.GND, Part5.GND, Part3.GND
  VCC: LCM1602_IIC2.VCC, Part5.5V, Part3.VCC
  N15: LCM1602_IIC2.SDA, Part5.A4/SDA
  N16: LCM1602_IIC2.SCL, Part5.A5/SCL
  N17: SD_card_module1.CS, Part4.RX2_LV
  N18: SD_card_module1.MOSI, Part4.TX2_LV
  N19: SD_card_module1.SCK, Part4.TX_LV
  N20: SD_card_module1.MISO, Part5.D12/MISO
  N21: Part4.LV, Part5.3V3
  N22: Part4.TX_HV, Part5.D13/SCK
  N23: Part4.RX2_HV, Part5.D4
  N24: Part4.TX2_HV, Part5.D11_PWM/MOSI
  N25: Part5.A0, Part3.OUT

custom parts:
  LCM1602 IIC: I2C-Module to use a 1602 or 2004 LCD on with the wire.h libory Serial LCD Modul
  SD Card Module: SD Card Module Slot Socket Reader For Arduino ARM MCU
