# Fritzing sketch soil_temperature_ds18b20 (saved by Fritzing 0.9.3b)
breadboards: 1

parts:
  Part9 = Arduino Uno (Rev3)
  LCM1602_IIC4 = LCM1602 IIC [part_number="LCM1602 IIC" chip_label="LCM1602 IIC" package="DIP (Dual Inline) [THT]"]
  LCD4 = LCD screen
  R2 = Resistor [tolerance=±5% resistance=4.7k package=THT]
  DS2 = DS18B20 1-Wire Temperature Sensor [part_number=DS18B20]

nets:
  N1: Part9.A4/SDA, LCM1602_IIC4.SDA
  N2: Part9.A5/SCL, LCM1602_IIC4.SCL
  N3: Part9.D3_PWM, R2.Pin_0, DS2.DQ
  5V: Part9.5V, LCM1602_IIC4.VCC, R2.Pin_1, DS2.VDD
  GND: Part9.GND, LCM1602_IIC4.GND, DS2.GND
  VSS: LCM1602_IIC4.VSS, LCD4.VSS
  VDD: LCM1602_IIC4.VDD, LCD4.VDD
  N4: LCM1602_IIC4.V0, LCD4.V0
  N5: LCM1602_IIC4.RS, LCD4.RS
  N6: LCM1602_IIC4.RW, LCD4.R/W
  N7: LCM1602_IIC4.E, LCD4.E
  N8: LCM1602_IIC4.D0, LCD4.DB0
  N9: LCM1602_IIC4.D1, LCD4.DB1
  N10: LCM1602_IIC4.D2, LCD4.DB2
  N11: LCM1602_IIC4.D3, LCD4.DB3
  N12: LCM1602_IIC4.D4, LCD4.DB4
  N13: LCM1602_IIC4.D5, LCD4.DB5
  N14: LCM1602_IIC4.D6, LCD4.DB6
  N15: LCM1602_IIC4.D7, LCD4.DB7
  N16: LCM1602_IIC4.A, LCD4.LED+
  N17: LCM1602_IIC4.K, LCD4.LED-

custom parts:
  LCM1602 IIC: I2C-Module to use a 1602 or 2004 LCD on with the wire.h libory Serial LCD Modul
